# Fritzing sketch OpenDispenserScheme (saved by Fritzing 0.9.3b)
breadboards: 1

parts:
  VCC2 = Battery  # not connected
  VCC4 = Battery
  VCC5 = Battery  # not connected
  VCC6 = Battery
  Componente1 = Arduino Uno (Rev3)
  L1 = Solenoid
  L2 = Solenoid
  L3 = Solenoid
  D1 = Diode [package=diode-1n4001]
  D2 = Diode [package=diode-1n4001]
  D3 = Diode [package=diode-1n4001]
  Q1 = npn-Powertransistor [package="TO220 [THT]"]
  Q2 = npn-Powertransistor [package="TO220 [THT]"]
  Q3 = npn-Powertransistor [package="TO220 [THT]"]
  R1 = Resistor [tolerance=±5% resistance=1k package="2010 [SMD]"]
  R2 = Resistor [tolerance=±5% resistance=1k package="2010 [SMD]"]
  R3 = Resistor [tolerance=±5% resistance=1k package="2010 [SMD]"]
  S1 = SWITCH-MOMENTARY-2 [package=reed_switch_pth]
  S3 = SWITCH-MOMENTARY-2 [package=reed_switch_pth]
  S2 = SWITCH-MOMENTARY-2 [package=reed_switch_pth]
  R4 = Resistor [tolerance=±5% resistance=220 package=THT]
  R5 = Resistor [tolerance=±5% resistance=220 package=THT]
  R6 = Resistor [tolerance=±5% resistance=220 package=THT]

nets:
  N1: VCC4.+, Componente1.VIN, L1.pin2, L2.pin2, L3.pin2, D1.C, D2.C, D3.C
  N2: VCC6.-, Componente1.GND, Q1.emitter, Q2.emitter, Q3.emitter, R4.Pin_1, R5.Pin_1, R6.Pin_1
  N3: Componente1.D11_PWM/MOSI, S3.2, R4.Pin_0
  N4: Componente1.D12/MISO, S2.2, R5.Pin_0
  N5: Componente1.D13/SCK, S1.2, R6.Pin_0
  N6: Componente1.D2, R3.Pin_1
  N7: Componente1.D3_PWM, R2.Pin_1
  N8: Componente1.D4, R1.Pin_1
  N9: Componente1.5V, S1.1, S3.1, S2.1
  N10: L1.pin1, Q1.collector
  N11: L2.pin1, Q2.collector
  N12: L3.pin1, Q3.collector
  N13: Q1.base, R1.Pin_0
  N14: Q2.base, R3.Pin_0
  N15: Q3.base, R2.Pin_0
